# Fritzing sketch ThermocoupleSenderPerfboard (saved by Fritzing 0.9.9b)
perfboards: 1

parts:
  U1 = ESP8266 NodeMCU LoLin module
  J2 = Camdenboss CTB0158-3 [part_number=CTB0158-3 package=THT]
  J3 = female pin header, 5 pins [form="♀ (female)"]
  U2 = mystery part, 5 pins [chip_label=RS-485]
  J4 = Camdenboss CTB0158-2 [part_number=CTB0158-2 package=THT]  # not connected
  U4 = mystery part, 5 pins [chip_label=MAX6675]
  J5 = female pin header, 5 pins [form="♀ (female)"]
  Y1 = CRYSTAL [part_number=hhh package=crystal-32khz-smd]  # not connected

nets:
  N1: U1.D1, J3.pin5, U2.pin5
  N2: U1.D4, J3.pin4, U2.pin4
  N3: U1.3V3, J2.pin1, J3.pin1, U2.pin1, U4.pin2, J5.pin4
  N4: U1.GND, J2.pin2, J3.pin2, U2.pin2, U4.pin1, J5.pin5
  N5: U1.D5, U4.pin3, J5.pin3
  N6: U1.D6, U4.pin5, J5.pin1
  N7: U1.D8, U4.pin4, J5.pin2
  N8: J3.pin3, U2.pin3

notes:
  A ~
  3V3
  B ~
  GnD
  TH1

custom parts:
  ESP8266 NodeMCU LoLin module: ESP8266 based NodeMCU
